# Fritzing sketch IHome (saved by Fritzing 0.9.3b)
breadboards: 1

parts:
  Part1 = Arduino Ethernet Shield (Rev3)
  Part2 = MQ-3 breakout
  LED1 = LEDs [package=led10mm]
  J1 = Piezo Speaker
  DHT1 = DHT11 Humitidy and Temperature Sensor

nets:
  N1: Part1.D8, DHT1.DATA
  GND: Part1.GND, Part2.GND, LED1.C, J1.pin1, DHT1.GND
  N2: Part1.A0, Part2.AO
  5V: Part1.5V, Part2.VCC, LED1.A, J1.pin2, DHT1.VDD

custom parts:
  MQ-3 breakout: Alcohol sensor is capable of detecting alcohol (ethanol) particles on itself and gives the information in digital form back to us to manipulate with it. SKU:101251 • Voltage: 5V DC • Power: max 750mW • Measurement range: 0.04-4mg/L
  DHT11 Humitidy and Temperature Sensor: DHT11 Humidity and Temperature Sensor
